# Fritzing sketch Schematic (saved by Fritzing 0.9.3b)
breadboards: 1

parts:
  U1 = NodeMCU V3.0
  LED1 = smd LED [color="Red (633nm)" package="1206 [SMD]"]
  Q1 = NPN-Transistor [package="TO92 [THT]"]
  R1 = Resistor [tolerance=±5% resistance=220 package="0603 [SMD]"]
  J1 = Infrared Proximity Sensor
  J2 = Piezo Speaker
  R2 = Photocell (LDR) [package=THT]
  R3 = Resistor [tolerance=±5% resistance=220 package="0603 [SMD]"]
  D1 = Rectifier Diode [part_number=1N4001 package="300 mil [THT]"]
  D2 = Rectifier Diode [part_number=1N4001 package="300 mil [THT]"]

nets (from the schematic view):
  N1: U1.D1, J1.Vcc
  N2: U1.D2, R2.pin_1
  N3: U1.GND#6, U1.GND#13, U1.GND#16, U1.GND#33, Q1.E, J1.GND, J2.pin1, R3.Pin_1
  N4: U1.D5, J2.pin2
  N5: U1.D6, R1.Pin_1
  N6: U1.VU, LED1.anode
  N7: U1.A0, D1.cathode, D2.cathode
  N8: LED1.cathode, Q1.C
  N9: Q1.B, R1.Pin_0
  N10: J1.Vout, D2.anode
  N11: R2.pin_0, R3.Pin_0, D1.anode

custom parts:
  NodeMCU V3.0: ESP8266 based NodeMCU
